# Fritzing sketch CO2 meter rev3 (saved by Fritzing 0.9.3b)
circuit board: 5cm x 7cm
breadboards: 2

parts:
  U1 = NodeMCU V1.0
  Squix1 = OLED 0.96" 128x64 I2C SSD1306 (GND/VCC)
  Squix2 = OLED 0.91" 128x32 I2C SSD1306 (GND/VCC)
  SPI&I2C = M16 [package=1x16_machine-pin-header_lock.004]
  I2C&SER = M16 [package=1x16_machine-pin-header_lock.004]
  TD-er1 = MH-Z19 CO2 sensor [part_number=MH-Z19]
  R1 = Resistor [tolerance=±5% resistance=10k package=THT]
  R2 = Resistor [tolerance=±5% resistance=10k package=THT]
  U2 = TOUCH [package=touch2]
  C1 = Capacitor Polarized [part_number=100uF25v package=cpol-radial-100uf-25v]
  C2 = Capacitor Polarized [part_number=100uF25v package=cpol-radial-100uf-25v]
  Pad1 = Pad [width=2 height=1 connect=center]
  Pad2 = Pad [width=2 height=1 connect=center]
  Pad3 = Pad [width=2 height=1 connect=center]
  Pad4 = Pad [width=2 height=1 connect=center]
  Pad5 = Pad [width=2 height=1 connect=center]
  Pad6 = Pad [width=2 height=1 connect=center]
  Pad7 = Pad [width=2 height=1 connect=center]
  Pad8 = Pad [width=2 height=1 connect=center]

nets:
  N1: U1.D1, Squix1.SCL, Squix2.SCL, SPI&I2C.3, SPI&I2C.8, SPI&I2C.11, I2C&SER.7, I2C&SER.12, I2C&SER.15, R1.Pin_0
  N2: U1.D2, Squix1.SCA, Squix2.SCA, SPI&I2C.4, SPI&I2C.7, SPI&I2C.12, I2C&SER.8, I2C&SER.11, I2C&SER.16, R2.Pin_0
  N3: U1.D3, I2C&SER.1, TD-er1.TX
  N4: U1.D4, I2C&SER.2, TD-er1.RX
  3.3V: U1.3V3, Squix1.VCC, Squix2.VCC, SPI&I2C.1, SPI&I2C.6, SPI&I2C.10, I2C&SER.5, I2C&SER.10, I2C&SER.14, R1.Pin_1, R2.Pin_1, U2.Vcc, C1.+
  GND: U1.GND, Squix1.GND, Squix2.GND, SPI&I2C.2, SPI&I2C.5, SPI&I2C.9, I2C&SER.4, I2C&SER.6, I2C&SER.9, I2C&SER.13, TD-er1.GND, U2.GND, C1.-, C2.-
  N5: U1.D5, SPI&I2C.13, Pad4.pad
  N6: U1.D6, SPI&I2C.14, Pad3.pad
  N7: U1.D7, SPI&I2C.15, Pad2.pad
  N8: U1.D8, SPI&I2C.16, Pad1.pad
  VIN: U1.Vin, I2C&SER.3, TD-er1.Vin, C2.+
  N9: U2.Out, Pad5.pad, Pad6.pad, Pad7.pad, Pad8.pad

notes:
  SDA
  SCL
  3V3
  GND
  5V
  RX
  TX
  HSCLK
  HMOSI
  HMISO
  HCS
  H-SPI
  I2C
  SER
  SCL:GPIO5(D1)
  SDA:GPIO4(D2)
  2017/11/17 v3
  TD-er.nl
  D3=TX
  pull-up
  D4=RX
  touch

custom parts:
  NodeMCU V1.0: ESP8266 based NodeMCU
  OLED 0.96" 128x64 I2C SSD1306 (GND/VCC): OLED 0.96" 128x64 I2C SSD1306 Pinout: GND/VCC/SCL/SDA
  OLED 0.91" 128x32 I2C SSD1306 (GND/VCC): OLED 0.91" 128x32 I2C SSD1306 Pinout: GND/VCC/SCL/SDA
  TOUCH: TTP223 Capacitive Touch Switch
